// Logisim project Circuit Lab.circ as structural Verilog: 3 circuits, main circuit main
module main (
  input  a,
  output [7:0] count,
  output clk_out,
  output y
);

  Clock clk (.out(clk_out));
  not not_1 (y, a);
  Counter_part #(.width(8)) cnt (.Q(count), .clk(clk_out));  // open: load, D, count, carry, up, clr
  RAM memory_ram ();  // open: addr, data, sel, clk, ld, clr
  ROM memory_rom ();  // open: addr, data

  // Notes on the sheet:
  //   contents of memory_rom (hex, n*v repeats v):
  //   1 2 3 4 5 6 7 8 9 a b c d e f 10 ff fe fd 4*0 aa 55
endmodule

module Counter (
  output [3:0] q
);

  wire subclk_out;

  Clock subclk (.out(subclk_out));
  Counter_part #(.width(4)) subcnt (.Q(q), .clk(subclk_out));  // open: load, D, count, carry, up, clr
  Register \reg  ();  // open: D, en, Q, clk, clr
endmodule

module Inverter (
  input  a,
  output y
);

  not not_1 (y, a);
endmodule
