// Logisim project ui-smoke.circ as structural Verilog: 5 circuits, main circuit main
module main (
  input  a,
  output [7:0] count,
  output clk_out,
  output y
);

  Clock clk (.out(clk_out));
  not not_1 (y, a);
  Counter #(.width(8)) cnt (.Q(count), .clk(clk_out));  // open: load, D, count, carry, up, clr
  RAM memory_ram ();  // open: addr, data, sel, clk, ld, clr
  ROM memory_rom ();  // open: addr, data
  counter_sub counter_sub_1 ();  // open: q

  // Notes on the sheet:
  //   contents of memory_rom (hex, n*v repeats v):
  //   1 2 3 4 5 6 7 8 9 a b c d e f 10 ff fe fd 4*0 aa 55
endmodule

module counter_sub (
  output [3:0] q
);

  wire subclk_out;

  Clock subclk (.out(subclk_out));
  Counter #(.width(4)) subcnt (.Q(q), .clk(subclk_out));  // open: load, D, count, carry, up, clr
  Register \reg  ();  // open: D, en, Q, clk, clr
endmodule

module inv (
  input  a,
  output y
);

  not not_1 (y, a);
endmodule

module osc (
);

  wire not_1_out;

  not not_1 (not_1_out, not_1_out);
endmodule

module mismatch (
  input  [3:0] in4,
  output [7:0] out8
);

  // Pins of 4 and 8 bits meet at {out8[7:4], in4}

  assign out8[3:0] = in4;
endmodule
